# Fritzing sketch MakerBuddy V1-0 (saved by Fritzing 1.0.2b)
circuit board: 7.23cm x 7.6cm
breadboards: 1

parts:
  32 = Dagu DGServo 9g header (male) [package=THT]
  26 = Dagu DGServo 9g header (male) [package=THT]
  33 = Dagu DGServo 9g header (male) [package=THT]
  25 = Dagu DGServo 9g header (male) [package=THT]
  UART = female pin header, 4 pins [form="♀ (female)"]
  5V = Header 2 [package=molex-1x2_lock]
  Push_BTN = Pushbutton [package="[THT]"]
  I2C = female pin header, 4 pins [form="♀ (female)"]
  23 = Dagu DGServo 9g header (male) [package=THT]
  19 = Dagu DGServo 9g header (male) [package=THT]
  18 = Dagu DGServo 9g header (male) [package=THT]
  M1 = DOIT Esp32 DevKit v1 (30 pins long, 11 pins width) [part_number=ESP32S-PIN30]
  J1 = female pin header, 15 pins [form="♀ (female)"]
  HC-SR04 = female pin header, 4 pins [form="♀ (female)"]
  10K = Resistor [tolerance=±5% resistance=4.7k power=0.25W package=THT]
  J2 = male pin header, 15 pins [form="♂ (male)"]
  4-Buzzer = Piezo Buzzer
  Cap = female pin header, 2 pins [form="♀ (female)"]
  34-Potentio = 6mm Trimmer Potentiometer [maximum_resistance=10kΩ knob_status=50% power=0.5W package=THT]
  4_7K = Resistor [tolerance=±5% power=0.25W resistance=4.7k package=THT]
  RGB = female pin header, 4 pins [form="♀ (female)"]
  12-LED = female pin header, 2 pins [form="♀ (female)"]
  35-LDR = female pin header, 2 pins [form="♀ (female)"]
  GND = female pin header, 4 pins [form="♀ (female)"]
  VCC = female pin header, 4 pins [form="♀ (female)"]
  I2C_2 = male pin header, 4 pins [form="♂ (male)"]
  I2C_3 = female pin header, 4 pins [form="♀ (female)"]

nets:
  N1: 32.gnd, M1.D32, J1.pin6
  VCC: 32.Vcc, 26.Vcc, 33.Vcc, 25.Vcc, UART.pin4, 5V.2, I2C.pin4, 23.Vcc, 19.Vcc, 18.Vcc, M1.VIN, J1.pin15, HC-SR04.pin4, Cap.pin1, 34-Potentio.leg2, 4_7K.Pin_1, RGB.pin3, 35-LDR.pin1, VCC.pin1, VCC.pin2, VCC.pin3, VCC.pin4, I2C_2.pin4, I2C_3.pin4
  N2: 32.pulse, 26.pulse, 33.pulse, 25.pulse, UART.pin3, 5V.1, Push_BTN.Pin_1, Push_BTN.Pin_2, I2C.pin3, 23.pulse, 19.pulse, 18.pulse, M1.GND, J1.pin14, HC-SR04.pin3, 10K.Pin_1, J2.pin14, 4-Buzzer.pin_2, Cap.pin2, 34-Potentio.leg1, 12-LED.pin1, GND.pin1, GND.pin2, GND.pin3, GND.pin4, I2C_2.pin3, I2C_3.pin3
  N3: 26.gnd, M1.D26, J1.pin9, 4_7K.Pin_0
  N4: 33.gnd, M1.D33, J1.pin7
  N5: 25.gnd, M1.D25, J1.pin8
  N6: UART.pin1, M1.RX2, J2.pin10
  N7: UART.pin2, M1.TX2, J2.pin9
  N8: Push_BTN.Pin_3, Push_BTN.Pin_4, M1.D5, J2.pin8
  N9: I2C.pin1, M1.D21, J2.pin5, I2C_2.pin1, I2C_3.pin1
  N10: I2C.pin2, M1.D22, J2.pin2, I2C_2.pin2, I2C_3.pin2
  N11: 23.gnd, M1.D23, J2.pin1
  N12: 19.gnd, M1.D19, J2.pin6
  N13: 18.gnd, M1.D18, J2.pin7
  N14: M1.3V3, J2.pin15
  N15: M1.D15, HC-SR04.pin1, J2.pin13
  N16: M1.D2, HC-SR04.pin2, J2.pin12
  N17: M1.D4, J2.pin11, 4-Buzzer.pin_1
  N18: M1.RX0, J2.pin4
  N19: M1.TX0, J2.pin3
  N20: M1.EN, J1.pin1
  N21: M1.VP, J1.pin2
  N22: M1.VN, J1.pin3
  N23: M1.D34, J1.pin4, 34-Potentio.wiper
  N24: M1.D35, J1.pin5, 10K.Pin_0, 35-LDR.pin2
  N25: M1.D27, J1.pin10, RGB.pin1
  N26: M1.D14, J1.pin11, RGB.pin2
  N27: M1.D12, J1.pin12, 12-LED.pin2
  N28: M1.D13, J1.pin13, RGB.pin4

notes:
  VCC
  GND
  SCL
  SDA
  TX
  RX
  15
  2
  12
  https://makerbuddy.cc
  27
  14
  13
  5

custom parts:
  DOIT Esp32 DevKit v1 (30 pins long, 11 pins width): The DOIT Esp32 DevKit v1 is one of the development board created by DOIT to evaluate the ESP-WROOM-32 module. It is based on the ESP32 microcontroller that boasts Wifi, Bluetooth, Ethernet and Low Power support all in a single chip. (vanepp) made breadboard work, adjusted pin numbering and labels and reduced size of schematic and cleaned up pcb. This chip is 30pins long (2 x15) and 11 pins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
  Piezo Buzzer: Part from https://www.nutsvolts.com/magazine/article/november2012_SmileysWorkshop. Breadboard and icon images modified to be 0.3" in spacing and be more similar to the actual physical part.
